# Fritzing sketch Theremidi Schematic (saved by Fritzing 0.9.3b)
breadboards: 1

parts:
  Pro_Micro6 = Pro Micro
  R1 = Resistor [tolerance=±5% resistance=14.87k package=THT]
  C1 = Ceramic Capacitor [capacitance=470nF package="200 mil [THT, multilayer]"]
  R2 = Resistor [tolerance=±5% resistance=14.87k package=THT]
  C2 = Ceramic Capacitor [capacitance="100 nF" package="200 mil [THT, multilayer]"]
  C3 = Ceramic Capacitor [capacitance=35µF package="200 mil [THT, multilayer]"]
  OLED1 = OLED 128x64 I2C Monochrome Display
  J3 = Infrared Proximity Sensor
  J4 = Infrared Proximity Sensor
  S1 = Pushbutton [package=THT]
  S2 = Pushbutton [package=THT]
  S3 = Pushbutton [package=THT]
  S4 = Pushbutton [package=THT]
  S5 = Pushbutton [package=THT]
  S6 = Pushbutton [package=THT]
  J5 = 1/4 inch mono jack [package=audio-jack-6.5mm-panel-mount]

nets:
  N1: Pro_Micro6.D2, OLED1.SDA
  N2: Pro_Micro6.D3, OLED1.SCK
  N3: Pro_Micro6.D4, S1.leg1
  N4: Pro_Micro6.D5, S4.leg1
  N5: Pro_Micro6.D6, S6.leg1
  N6: Pro_Micro6.D7, S2.leg1
  N7: Pro_Micro6.D8, S3.leg1
  N8: Pro_Micro6.D9, S5.leg1
  N9: Pro_Micro6.D10, J5.Tip
  N10: Pro_Micro6.D18/A0, R1.Pin_0, C1.0
  N11: Pro_Micro6.D19/A1, R2.Pin_0, C2.0
  VCC: Pro_Micro6.VCC, C3.0, OLED1.VDD, J3.Vcc, J4.Vcc
  GND: Pro_Micro6.GND, C1.1, C2.1, C3.1, OLED1.GND, J3.GND, J4.GND, S1.leg0, S2.leg0, S3.leg0, S4.leg0, S5.leg0, S6.leg0, J5.Sleeve
  N12: R1.Pin_1, J3.Vout
  N13: R2.Pin_1, J4.Vout

notes:
  35uF
  0.47uF
  14.87k
  Sharp GP2Y0A41SK0F
  OLED Display (128x64)
  Arduino Pro Micro
  Sustain
  Mono 1/4 Audio Jack

custom parts:
  Pro Micro: The SparkFun Pro Micro is a complete USB-based microcontoller development system, in a very small footprint, capable of implementing many types of projects. All programming can be done via the USB port.
  1/4 inch mono jack: 1/4 inch mono Audio Jack Simple 1/4 inch panel mount audio jack.
